// Logisim project ALU_circuit.circ as structural Verilog: 1 circuit, main circuit ALU
module ALU (
  input  n_ot,
  input  o_r,
  input  a_nd,
  input  div,
  input  mul,
  input  sub,
  input  add,
  input  ao_enable,
  input  clk,
  input  [15:0] in1,
  input  [15:0] in2,
  output [15:0] ao,
  output [15:0] fl,
  output fl_clk
);

  wire adder_1_cout, nor_1_out, not_2_out, not_3_out, not_4_out, not_5_out, not_6_out, not_7_out, not_8_out,
       subtractor_1_bout;
  wire [15:0] adder_1_out, and_1_out, bit_extender_1_out, bit_extender_2_out, controlled_buffer_1_out,
       divider_1_out, divider_1_rem, multiplier_1_cout, multiplier_1_out, not_1_out, or_1_out,
       subtractor_1_out;

  Adder #(.width(16)) adder_1 (.a(in1), .b(in2), .out(adder_1_out), .cout(adder_1_cout));  // open: cin
  Subtractor #(.width(16)) subtractor_1 (
    .a(in1), .b(in2), .out(subtractor_1_out), .bout(subtractor_1_bout));  // open: bin
  assign bit_extender_1_out = {{15{1'b0}}, adder_1_cout};  // Bit_Extender bit_extender_1
  assign controlled_buffer_1_out = add ? adder_1_out : 16'bz;  // Controlled_Buffer controlled_buffer_1
  assign controlled_buffer_1_out = sub ? subtractor_1_out : 16'bz;  // Controlled_Buffer controlled_buffer_2
  assign controlled_buffer_1_out = mul ? multiplier_1_out : 16'bz;  // Controlled_Buffer controlled_buffer_3
  Multiplier #(.width(16)) multiplier_1 (
    .a(in1), .b(in1), .out(multiplier_1_out), .cout(multiplier_1_cout));  // open: cin
  assign bit_extender_2_out = {{15{1'b0}}, subtractor_1_bout};  // Bit_Extender bit_extender_2
  assign controlled_buffer_1_out = div ? divider_1_out : 16'bz;  // Controlled_Buffer controlled_buffer_4
  assign controlled_buffer_1_out = a_nd ? and_1_out : 16'bz;  // Controlled_Buffer controlled_buffer_5
  assign controlled_buffer_1_out = o_r ? or_1_out : 16'bz;  // Controlled_Buffer controlled_buffer_6
  assign and_1_out = in1 & in2;  // AND_Gate and_1, 16 bits wide
  assign or_1_out = in1 | in2;  // OR_Gate or_1, 16 bits wide
  Divider #(.width(16)) divider_1 (.a(in1), .b(in2), .out(divider_1_out), .rem(divider_1_rem));  // open: upper
  assign fl = div ? divider_1_rem : 16'bz;  // Controlled_Buffer controlled_buffer_7
  assign fl = mul ? multiplier_1_cout : 16'bz;  // Controlled_Buffer controlled_buffer_8
  assign fl = sub ? bit_extender_2_out : 16'bz;  // Controlled_Buffer controlled_buffer_9
  assign fl = add ? bit_extender_1_out : 16'bz;  // Controlled_Buffer controlled_buffer_10
  assign fl = nor_1_out ? {16{1'b0}} : 16'bz;  // Controlled_Buffer controlled_buffer_11
  nor nor_1 (nor_1_out, div, mul, sub, add);
  Register #(.width(16)) register_1 (.D(controlled_buffer_1_out), .en(ao_enable), .clk(clk), .Q(ao));  // open: clr
  assign controlled_buffer_1_out = n_ot ? not_1_out : 16'bz;  // Controlled_Buffer controlled_buffer_12
  assign not_1_out = ~in1;  // NOT_Gate not_1, 16 bits wide
  not not_2 (not_2_out, clk);
  not not_3 (not_3_out, not_2_out);
  not not_4 (not_4_out, not_3_out);
  not not_5 (not_5_out, not_4_out);
  not not_6 (not_6_out, not_5_out);
  not not_7 (not_7_out, not_6_out);
  not not_8 (not_8_out, not_7_out);
  not not_9 (fl_clk, not_8_out);
endmodule
