// Logisim project T16b2.circ as structural Verilog
module main (
  input  in_1,
  input  [5:0] in_2,
  input  in_3
);

  wire a_out, b_out, backspace_out, c_out, d_out, e_out, f_out, g_out, h_out, i_out, j_out, k_out,
       keyboard_controller_1_out_tty_clk, l_out, m_out, n_out, o_out, p_out, q_out, r_out, s_out, space_out,
       t_out, u_out, v_out, w_out, x_out, y_out, z_out;
  wire [6:0] keyboard_controller_1_keyboard_out, keyboard_controller_1_out_tty_data;

  TTY #(.cols(72), .rows(16)) tty_1 (
    .data(keyboard_controller_1_out_tty_data), .clk(keyboard_controller_1_out_tty_clk));  // open: we, clr
  keyboard_controller keyboard_controller_1 (
    .a(a_out), .b(b_out), .c(c_out), .d(d_out), .e(e_out), .f(f_out), .g(g_out), .h(h_out), .i(i_out),
    .j(j_out), .k(k_out), .l(l_out), .m(m_out), .n(n_out), .o(o_out), .p(p_out), .q(q_out), .r(r_out),
    .s(s_out), .t(t_out), .u(u_out), .v(v_out), .w(w_out), .x(x_out), .y(y_out), .z(z_out),
    .space(space_out), .backspace(backspace_out), .output_clk(in_3), .keyboard_mem_addr(in_2),
    .output_enable(in_1), .keyboard_out(keyboard_controller_1_keyboard_out),
    .out_tty_data(keyboard_controller_1_out_tty_data), .out_tty_clk(keyboard_controller_1_out_tty_clk));
  Button q (.out(q_out));
  Button w (.out(w_out));
  Button a (.out(a_out));
  Button s (.out(s_out));
  Button z (.out(z_out));
  Button e (.out(e_out));
  Button r (.out(r_out));
  Button t (.out(t_out));
  Button d (.out(d_out));
  Button f (.out(f_out));
  Button x (.out(x_out));
  Button c (.out(c_out));
  Button v (.out(v_out));
  Button space (.out(space_out));
  Button y (.out(y_out));
  Button u (.out(u_out));
  Button g (.out(g_out));
  Button h (.out(h_out));
  Button j (.out(j_out));
  Button b (.out(b_out));
  Button n (.out(n_out));
  Button backspace (.out(backspace_out));
  Button i (.out(i_out));
  Button o (.out(o_out));
  Button p (.out(p_out));
  Button k (.out(k_out));
  Button l (.out(l_out));
  Button m (.out(m_out));
  // Probe on keyboard_controller_1_keyboard_out
endmodule

module ALU (
  input  n_ot,
  input  o_r,
  input  a_nd,
  input  div,
  input  mul,
  input  sub,
  input  add,
  input  ao_enable,
  input  clk,
  input  [15:0] in1,
  input  [15:0] in2,
  output [15:0] ao,
  output [15:0] fl,
  output fl_clk
);

  wire adder_1_cout, nor_1_out, not_2_out, not_3_out, not_4_out, not_5_out, not_6_out, not_7_out, not_8_out,
       subtractor_1_bout;
  wire [15:0] adder_1_out, and_1_out, bit_extender_1_out, bit_extender_2_out, controlled_buffer_1_out,
       divider_1_out, divider_1_rem, multiplier_1_cout, multiplier_1_out, not_1_out, or_1_out,
       subtractor_1_out;

  Adder #(.width(16)) adder_1 (.a(in1), .b(in2), .out(adder_1_out), .cout(adder_1_cout));  // open: cin
  assign controlled_buffer_1_out = add ? adder_1_out : 16'bz;  // Controlled_Buffer controlled_buffer_1
  assign controlled_buffer_1_out = sub ? subtractor_1_out : 16'bz;  // Controlled_Buffer controlled_buffer_2
  Subtractor #(.width(16)) subtractor_1 (
    .a(in1), .b(in2), .out(subtractor_1_out), .bout(subtractor_1_bout));  // open: bin
  Multiplier #(.width(16)) multiplier_1 (
    .a(in1), .b(in1), .out(multiplier_1_out), .cout(multiplier_1_cout));  // open: cin
  assign bit_extender_1_out = {{15{1'b0}}, subtractor_1_bout};  // Bit_Extender bit_extender_1
  assign bit_extender_2_out = {{15{1'b0}}, adder_1_cout};  // Bit_Extender bit_extender_2
  assign controlled_buffer_1_out = mul ? multiplier_1_out : 16'bz;  // Controlled_Buffer controlled_buffer_3
  assign controlled_buffer_1_out = div ? divider_1_out : 16'bz;  // Controlled_Buffer controlled_buffer_4
  Divider #(.width(16)) divider_1 (.a(in1), .b(in2), .out(divider_1_out), .rem(divider_1_rem));  // open: upper
  assign controlled_buffer_1_out = a_nd ? and_1_out : 16'bz;  // Controlled_Buffer controlled_buffer_5
  assign controlled_buffer_1_out = o_r ? or_1_out : 16'bz;  // Controlled_Buffer controlled_buffer_6
  assign controlled_buffer_1_out = n_ot ? not_1_out : 16'bz;  // Controlled_Buffer controlled_buffer_7
  assign and_1_out = in1 & in2;  // AND_Gate and_1, 16 bits wide
  assign or_1_out = in1 | in2;  // OR_Gate or_1, 16 bits wide
  assign not_1_out = ~in1;  // NOT_Gate not_1, 16 bits wide
  assign fl = div ? divider_1_rem : 16'bz;  // Controlled_Buffer controlled_buffer_8
  assign fl = mul ? multiplier_1_cout : 16'bz;  // Controlled_Buffer controlled_buffer_9
  assign fl = sub ? bit_extender_1_out : 16'bz;  // Controlled_Buffer controlled_buffer_10
  assign fl = add ? bit_extender_2_out : 16'bz;  // Controlled_Buffer controlled_buffer_11
  assign fl = nor_1_out ? {16{1'b0}} : 16'bz;  // Controlled_Buffer controlled_buffer_12
  nor nor_1 (nor_1_out, div, mul, sub, add);
  Register #(.width(16)) register_1 (.D(controlled_buffer_1_out), .en(ao_enable), .clk(clk), .Q(ao));  // open: clr
  not not_2 (not_2_out, clk);
  not not_3 (not_3_out, not_2_out);
  not not_4 (not_4_out, not_3_out);
  not not_5 (not_5_out, not_4_out);
  not not_6 (not_6_out, not_5_out);
  not not_7 (not_7_out, not_6_out);
  not not_8 (not_8_out, not_7_out);
  not not_9 (fl_clk, not_8_out);
endmodule

module keyboard_controller (
  input  [5:0] keyboard_mem_addr,
  input  output_enable,
  input  a,
  input  b,
  input  c,
  input  d,
  input  e,
  input  f,
  input  g,
  input  output_clk,
  input  h,
  input  i,
  input  j,
  input  k,
  input  l,
  input  m,
  input  n,
  input  o,
  input  p,
  input  q,
  input  r,
  input  s,
  input  t,
  input  u,
  input  v,
  input  w,
  input  x,
  input  y,
  input  space,
  input  z,
  input  backspace,
  output [6:0] keyboard_out,
  output [6:0] out_tty_data,
  output out_tty_clk
);

  wire comparator_1_eq, controlled_buffer_30_out, not_1_out, not_2_out, not_3_out, not_4_out, not_5_out,
       not_6_out, not_7_out, not_8_out, not_9_out, not_10_out, not_11_out, not_12_out, not_13_out,
       not_14_out, not_15_out, not_16_out, not_17_out, not_18_out, not_19_out, not_20_out, not_21_out,
       not_22_out, not_23_out, not_24_out, not_25_out, not_26_out, not_27_out, not_28_out, not_29_out,
       not_30_out, not_31_out, not_32_out, not_33_out, not_34_out, not_35_out, not_36_out, not_37_out,
       not_38_out, not_39_out, not_40_out, not_41_out, not_42_out;
  wire [5:0] counter_1_q, multiplexer_2_out;
  wire [6:0] multiplexer_1_out, register_1_q;

  assign out_tty_data = a ? 7'b1100001 : 7'bz;  // Controlled_Buffer controlled_buffer_1
  assign out_tty_data = b ? 7'b1100010 : 7'bz;  // Controlled_Buffer controlled_buffer_2
  assign out_tty_data = c ? 7'b1100011 : 7'bz;  // Controlled_Buffer controlled_buffer_3
  assign out_tty_data = d ? 7'b1100100 : 7'bz;  // Controlled_Buffer controlled_buffer_4
  assign out_tty_data = e ? 7'b1100101 : 7'bz;  // Controlled_Buffer controlled_buffer_5
  assign out_tty_data = f ? 7'b1100110 : 7'bz;  // Controlled_Buffer controlled_buffer_6
  assign out_tty_data = g ? 7'b1100111 : 7'bz;  // Controlled_Buffer controlled_buffer_7
  assign out_tty_data = h ? 7'b1101000 : 7'bz;  // Controlled_Buffer controlled_buffer_8
  assign out_tty_data = i ? 7'b1101001 : 7'bz;  // Controlled_Buffer controlled_buffer_9
  assign out_tty_data = j ? 7'b1101010 : 7'bz;  // Controlled_Buffer controlled_buffer_10
  assign out_tty_data = k ? 7'b1101011 : 7'bz;  // Controlled_Buffer controlled_buffer_11
  assign out_tty_data = l ? 7'b1101100 : 7'bz;  // Controlled_Buffer controlled_buffer_12
  assign out_tty_data = m ? 7'b1101101 : 7'bz;  // Controlled_Buffer controlled_buffer_13
  assign out_tty_data = n ? 7'b1101110 : 7'bz;  // Controlled_Buffer controlled_buffer_14
  assign out_tty_data = o ? 7'b1101111 : 7'bz;  // Controlled_Buffer controlled_buffer_15
  assign out_tty_data = p ? 7'b1110000 : 7'bz;  // Controlled_Buffer controlled_buffer_16
  assign out_tty_data = q ? 7'b1110001 : 7'bz;  // Controlled_Buffer controlled_buffer_17
  assign out_tty_data = r ? 7'b1110010 : 7'bz;  // Controlled_Buffer controlled_buffer_18
  assign out_tty_data = s ? 7'b1110011 : 7'bz;  // Controlled_Buffer controlled_buffer_19
  assign out_tty_data = t ? 7'b1110100 : 7'bz;  // Controlled_Buffer controlled_buffer_20
  assign out_tty_data = u ? 7'b1110101 : 7'bz;  // Controlled_Buffer controlled_buffer_21
  assign out_tty_data = v ? 7'b1110110 : 7'bz;  // Controlled_Buffer controlled_buffer_22
  assign out_tty_data = w ? 7'b1110111 : 7'bz;  // Controlled_Buffer controlled_buffer_23
  assign out_tty_data = x ? 7'b1111000 : 7'bz;  // Controlled_Buffer controlled_buffer_24
  assign out_tty_data = y ? 7'b1111001 : 7'bz;  // Controlled_Buffer controlled_buffer_25
  assign out_tty_data = z ? 7'b1111010 : 7'bz;  // Controlled_Buffer controlled_buffer_26
  Pull_Resistor pull_resistor_1 (.node(out_tty_data));
  assign out_tty_data = space ? 7'b0100000 : 7'bz;  // Controlled_Buffer controlled_buffer_27
  assign out_tty_data = backspace ? 7'b0001000 : 7'bz;  // Controlled_Buffer controlled_buffer_28
  not not_1 (not_1_out, not_4_out);
  not not_2 (not_2_out, not_12_out);
  Multiplexer #(.width(7)) multiplexer_1 (
    .in0(out_tty_data), .in1({7{1'b0}}), .out(multiplexer_1_out), .sel(backspace));
  Register #(.width(7)) register_1 (.D(multiplexer_1_out), .clk(not_3_out), .Q(register_1_q));  // open: en, clr
  not not_3 (not_3_out, comparator_1_eq);
  Comparator #(.mode("unsigned"), .width(7)) comparator_1 (
    .a(out_tty_data), .b({7{1'b0}}), .eq(comparator_1_eq));  // open: gt, lt
  not not_4 (not_4_out, not_5_out);
  not not_5 (not_5_out, not_6_out);
  not not_6 (not_6_out, not_7_out);
  not not_7 (not_7_out, not_22_out);
  not not_8 (not_8_out, not_2_out);
  not not_9 (not_9_out, not_8_out);
  not not_10 (not_10_out, not_9_out);
  not not_11 (not_11_out, not_10_out);
  not not_12 (not_12_out, not_13_out);
  not not_13 (not_13_out, not_14_out);
  not not_14 (not_14_out, not_15_out);
  not not_15 (not_15_out, not_29_out);
  not not_16 (not_16_out, backspace);
  not not_17 (not_17_out, not_16_out);
  not not_18 (not_18_out, not_17_out);
  not not_19 (not_19_out, not_18_out);
  not not_20 (not_20_out, not_21_out);
  not not_21 (not_21_out, not_3_out);
  Pull_Resistor pull_resistor_2 (.node(out_tty_clk));
  assign out_tty_clk = not_39_out ? not_3_out : 1'bz;  // Controlled_Buffer controlled_buffer_29
  not not_22 (not_22_out, not_23_out);
  not not_23 (not_23_out, not_24_out);
  not not_24 (not_24_out, not_28_out);
  not not_25 (not_25_out, not_11_out);
  not not_26 (not_26_out, not_25_out);
  not not_27 (not_27_out, not_26_out);
  not not_28 (not_28_out, not_27_out);
  not not_29 (not_29_out, not_30_out);
  not not_30 (not_30_out, not_31_out);
  not not_31 (not_31_out, not_35_out);
  not not_32 (not_32_out, not_19_out);
  not not_33 (not_33_out, not_32_out);
  not not_34 (not_34_out, not_33_out);
  not not_35 (not_35_out, not_34_out);
  not not_36 (not_36_out, not_20_out);
  not not_37 (not_37_out, not_36_out);
  not not_38 (not_38_out, not_37_out);
  not not_39 (not_39_out, output_enable);
  not not_40 (not_40_out, not_1_out);
  Counter #(.max('h3f), .width(6)) counter_1 (
    .load(output_enable), .D(counter_1_q), .Q(counter_1_q), .up(not_40_out), .clk(not_38_out));  // open: count, carry, clr
  not not_41 (not_41_out, output_enable);
  assign controlled_buffer_30_out = output_enable ? output_clk : 1'bz;  // Controlled_Buffer controlled_buffer_30
  Multiplexer #(.width(6)) multiplexer_2 (
    .in0(counter_1_q), .in1(keyboard_mem_addr), .out(multiplexer_2_out), .sel(output_enable));
  not not_42 (not_42_out, output_enable);
  assign controlled_buffer_30_out = not_41_out ? not_38_out : 1'bz;  // Controlled_Buffer controlled_buffer_31
  RAM #(.addrWidth(6), .dataWidth(7)) ram_1 (
    .addr(multiplexer_2_out), .we(not_42_out), .oe(output_enable), .clk(controlled_buffer_30_out),
    .din(register_1_q), .dout(keyboard_out));
endmodule

module seventoeightbit (
  input  [6:0] in_1,
  input  [6:0] in_2,
  input  [6:0] in_3,
  input  [6:0] in_4,
  input  [6:0] in_5,
  input  [6:0] in_6,
  input  [6:0] in_7,
  input  [6:0] in_8,
  input  [6:0] in_9,
  input  [6:0] in_10,
  input  [6:0] in_11,
  input  [6:0] in_12,
  input  [6:0] in_13,
  input  [6:0] in_14,
  input  [6:0] in_15,
  input  [6:0] in_16,
  input  [6:0] in_17,
  input  [6:0] in_18,
  input  [6:0] in_19,
  input  [6:0] in_20,
  input  [6:0] in_21,
  input  [6:0] in_22,
  input  [6:0] in_23,
  input  [6:0] in_24,
  input  [6:0] in_25,
  input  [6:0] in_26,
  input  [6:0] in_27,
  input  [6:0] in_28,
  input  [6:0] in_29,
  input  [6:0] in_30,
  input  [6:0] in_31,
  input  [6:0] in_32,
  input  [6:0] in_33,
  input  [6:0] in_34,
  input  [6:0] in_35,
  input  [6:0] in_36,
  input  [6:0] in_37,
  input  [6:0] in_38,
  input  [6:0] in_39,
  input  [6:0] in_40,
  input  [6:0] in_41,
  input  [6:0] in_42,
  input  [6:0] in_43,
  input  [6:0] in_44,
  input  [6:0] in_45,
  output [7:0] out_46,
  output [7:0] out_47,
  output [7:0] out_48,
  output [7:0] out_49,
  output [7:0] out_50,
  output [7:0] out_51,
  output [7:0] out_52,
  output [7:0] out_53,
  output [7:0] out_54,
  output [7:0] out_55,
  output [7:0] out_56,
  output [7:0] out_57,
  output [7:0] out_58,
  output [7:0] out_59,
  output [7:0] out_60,
  output [7:0] out_61,
  output [7:0] out_62,
  output [7:0] out_63,
  output [7:0] out_64,
  output [7:0] out_65,
  output [7:0] out_66,
  output [7:0] out_67,
  output [7:0] out_68,
  output [7:0] out_69,
  output [7:0] out_70,
  output [7:0] out_71,
  output [7:0] out_72,
  output [7:0] out_73,
  output [7:0] out_74,
  output [7:0] out_75,
  output [7:0] out_76,
  output [7:0] out_77,
  output [7:0] out_78,
  output [7:0] out_79,
  output [7:0] out_80,
  output [7:0] out_81,
  output [7:0] out_82,
  output [7:0] out_83,
  output [7:0] out_84,
  output [7:0] out_85,
  output [7:0] out_86,
  output [7:0] out_87,
  output [7:0] out_88,
  output [7:0] out_89,
  output [7:0] out_90
);

  assign out_46 = {{1{in_1[6]}}, in_1};  // Bit_Extender bit_extender_1
  assign out_49 = {{1{in_4[6]}}, in_4};  // Bit_Extender bit_extender_2
  assign out_52 = {{1{in_7[6]}}, in_7};  // Bit_Extender bit_extender_3
  assign out_55 = {{1{in_10[6]}}, in_10};  // Bit_Extender bit_extender_4
  assign out_58 = {{1{in_13[6]}}, in_13};  // Bit_Extender bit_extender_5
  assign out_61 = {{1{in_16[6]}}, in_16};  // Bit_Extender bit_extender_6
  assign out_64 = {{1{in_19[6]}}, in_19};  // Bit_Extender bit_extender_7
  assign out_67 = {{1{in_22[6]}}, in_22};  // Bit_Extender bit_extender_8
  assign out_70 = {{1{in_25[6]}}, in_25};  // Bit_Extender bit_extender_9
  assign out_73 = {{1{in_28[6]}}, in_28};  // Bit_Extender bit_extender_10
  assign out_76 = {{1{in_31[6]}}, in_31};  // Bit_Extender bit_extender_11
  assign out_79 = {{1{in_34[6]}}, in_34};  // Bit_Extender bit_extender_12
  assign out_82 = {{1{in_37[6]}}, in_37};  // Bit_Extender bit_extender_13
  assign out_85 = {{1{in_40[6]}}, in_40};  // Bit_Extender bit_extender_14
  assign out_87 = {{1{in_42[6]}}, in_42};  // Bit_Extender bit_extender_15
  assign out_89 = {{1{in_44[6]}}, in_44};  // Bit_Extender bit_extender_16
  assign out_47 = {{1{in_2[6]}}, in_2};  // Bit_Extender bit_extender_17
  assign out_50 = {{1{in_5[6]}}, in_5};  // Bit_Extender bit_extender_18
  assign out_53 = {{1{in_8[6]}}, in_8};  // Bit_Extender bit_extender_19
  assign out_56 = {{1{in_11[6]}}, in_11};  // Bit_Extender bit_extender_20
  assign out_59 = {{1{in_14[6]}}, in_14};  // Bit_Extender bit_extender_21
  assign out_62 = {{1{in_17[6]}}, in_17};  // Bit_Extender bit_extender_22
  assign out_65 = {{1{in_20[6]}}, in_20};  // Bit_Extender bit_extender_23
  assign out_68 = {{1{in_23[6]}}, in_23};  // Bit_Extender bit_extender_24
  assign out_71 = {{1{in_26[6]}}, in_26};  // Bit_Extender bit_extender_25
  assign out_74 = {{1{in_29[6]}}, in_29};  // Bit_Extender bit_extender_26
  assign out_77 = {{1{in_32[6]}}, in_32};  // Bit_Extender bit_extender_27
  assign out_80 = {{1{in_35[6]}}, in_35};  // Bit_Extender bit_extender_28
  assign out_83 = {{1{in_38[6]}}, in_38};  // Bit_Extender bit_extender_29
  assign out_86 = {{1{in_41[6]}}, in_41};  // Bit_Extender bit_extender_30
  assign out_88 = {{1{in_43[6]}}, in_43};  // Bit_Extender bit_extender_31
  assign out_90 = {{1{in_45[6]}}, in_45};  // Bit_Extender bit_extender_32
  assign out_48 = {{1{in_3[6]}}, in_3};  // Bit_Extender bit_extender_33
  assign out_51 = {{1{in_6[6]}}, in_6};  // Bit_Extender bit_extender_34
  assign out_54 = {{1{in_9[6]}}, in_9};  // Bit_Extender bit_extender_35
  assign out_57 = {{1{in_12[6]}}, in_12};  // Bit_Extender bit_extender_36
  assign out_60 = {{1{in_15[6]}}, in_15};  // Bit_Extender bit_extender_37
  assign out_63 = {{1{in_18[6]}}, in_18};  // Bit_Extender bit_extender_38
  assign out_66 = {{1{in_21[6]}}, in_21};  // Bit_Extender bit_extender_39
  assign out_69 = {{1{in_24[6]}}, in_24};  // Bit_Extender bit_extender_40
  assign out_72 = {{1{in_27[6]}}, in_27};  // Bit_Extender bit_extender_41
  assign out_75 = {{1{in_30[6]}}, in_30};  // Bit_Extender bit_extender_42
  assign out_78 = {{1{in_33[6]}}, in_33};  // Bit_Extender bit_extender_43
  assign out_81 = {{1{in_36[6]}}, in_36};  // Bit_Extender bit_extender_44
  assign out_84 = {{1{in_39[6]}}, in_39};  // Bit_Extender bit_extender_45
endmodule
